// Logisim project Cache.circ as structural Verilog
module main (
  input  EnableTestHalting,
  output [9:0] CorrectCounter,
  output [9:0] HitCounter,
  output [9:0] MissCounter,
  output [9:0] TestNumber,
  output [7:0] ByteRead,
  output [7:0] CorrectByteRead,
  output Halt
);

  wire and_3_out, and_4_out, and_5_out, CLK, CmdIsRead, Correct, CpuRead, CpuWrite, DidContain, HaltTesting,
       MaxItersReached, MemRead, MemWrite, not_1_out, not_2_out, not_4_out, NotDoneTesting, Ok2Count,
       or_1_out, Ready;
  wire [7:0] CpuWriteValue, MemAddress;
  wire [9:0] CpuAddress;
  wire [31:0] Line2Mem, LineFromMem;

  not not_1 (not_1_out, Ready);
  Clock clock_1 (.out(CLK));
  or or_1 (or_1_out, MaxItersReached, Ready);
  Counter #(.width(4), .max('h9)) MaxClocks (
    .load(Ready), .D(4'b0001), .count(not_1_out), .carry(MaxItersReached), .clk(CLK));  // open: Q, clr
  and and_1 (HaltTesting, EnableTestHalting, CmdIsRead, not_2_out);
  not not_2 (not_2_out, Correct);
  not not_3 (NotDoneTesting, Halt);
  Inputs inputs_1 (
    .HaltTesting(HaltTesting), .Ready(or_1_out), .CLK(CLK), .Done(Halt), .Read(CpuRead), .Write(CpuWrite),
    .Address(CpuAddress), .Value(CpuWriteValue), .TestNumber(TestNumber));
  Cache cache_1 (
    .CpuAddress(CpuAddress), .CpuRead(CpuRead), .CpuWrite(CpuWrite), .CpuWriteValue(CpuWriteValue),
    .CLK(CLK), .Ready(Ready), .DidContain(DidContain), .ByteRead(ByteRead), .MemAddress(MemAddress),
    .MemRead(MemRead), .MemWrite(MemWrite), .LineFromMem(LineFromMem), .Line2Mem(Line2Mem));
  // Probe on CpuRead
  // Probe on CpuWrite
  // Probe on CpuAddress
  // Probe on CpuWriteValue
  // Probe on TestNumber
  // Probe on CorrectByteRead
  // Probe on Correct
  // Probe on Ready
  // Probe on DidContain
  // Probe on ByteRead
  // Probe on MemAddress
  // Probe on MemRead
  // Probe on MemWrite
  // Probe on HitCounter
  // Probe on LineFromMem
  // Probe on Line2Mem
  not not_4 (not_4_out, HaltTesting);
  RAM #(.dataWidth(32), .bus("separate")) ram_1 (
    .addr(MemAddress), .din(Line2Mem), .data(LineFromMem), .str(MemWrite), .clk(CLK), .ld(MemRead));  // open: sel, clr
  and and_2 (Ok2Count, Ready, not_4_out, NotDoneTesting);
  and and_3 (and_3_out, Correct, Ok2Count);
  and and_4 (and_4_out, DidContain, Ok2Count);
  and and_5 (and_5_out, MemRead, NotDoneTesting);
  Checker checker_1 (
    .TestNumber(TestNumber), .YourByteRead(ByteRead), .CmdIsRead(CmdIsRead),
    .CorrectByteRead(CorrectByteRead), .Correct(Correct));
  Counter #(.width(10), .max('h3ff)) u_CorrectCounter (
    .count(and_3_out), .Q(CorrectCounter), .clk(CLK));  // open: load, D, carry, clr
  Counter #(.width(10), .max('h3ff)) u_HitCounter (
    .count(and_4_out), .Q(HitCounter), .clk(CLK));  // open: load, D, carry, clr
  Counter #(.width(10), .max('h3ff)) u_MissCounter (
    .count(and_5_out), .Q(MissCounter), .clk(CLK));  // open: load, D, carry, clr
  // Probe on CorrectCounter
  // Probe on HitCounter
  // Probe on MissCounter

  // Other names for the same wires on the sheet: DoneTesting = Halt

  // Notes on the sheet:
  //   Your Answer Inside Here
endmodule

module Cache (
  input  [9:0] CpuAddress,
  input  CpuRead,
  input  CpuWrite,
  input  [7:0] CpuWriteValue,
  input  CLK,
  input  [31:0] LineFromMem,
  output Ready,
  output DidContain,
  output [7:0] ByteRead,
  output [7:0] MemAddress,
  output MemRead,
  output MemWrite,
  output [31:0] Line2Mem
);

  wire DidDirtyBit, ReadFromSet0, ReadFromSet1, Set0Contains, Set0DirtyBit, Set1Contains, Set1DirtyBit,
       WriteToSet0, WriteToSet1;
  wire [1:0] LineIterator, OffsetToSet0, OffsetToSet1;
  wire [2:0] WhichLine, WhichLineSet0, WhichLineSet1;
  wire [6:0] Set0StoreTag, Set1StoreTag, TagToSet0, TagToSet1;
  wire [7:0] Set0ByteRead, Set1ByteRead;
  wire [31:0] MemToSet0, MemToSet1, Set0Line2Mem, Set1Line2Mem;

  Demultiplexer #(.width(7), .enable("false")) demultiplexer_1 (
    .out0(TagToSet0), .out1(TagToSet1), .in(CpuAddress[9:3]), .sel(CpuAddress[2]));
  Demultiplexer #(.width(2), .enable("false")) demultiplexer_2 (
    .out0(OffsetToSet0), .out1(OffsetToSet1), .in(CpuAddress[1:0]), .sel(CpuAddress[2]));
  Demultiplexer #(.enable("false")) demultiplexer_3 (
    .out0(ReadFromSet0), .out1(ReadFromSet1), .in(CpuRead), .sel(CpuAddress[2]));
  Demultiplexer #(.enable("false")) demultiplexer_4 (
    .out0(WriteToSet0), .out1(WriteToSet1), .in(CpuWrite), .sel(CpuAddress[2]));
  Demultiplexer #(.width(32), .enable("false")) demultiplexer_5 (
    .out0(MemToSet0), .out1(MemToSet1), .in(LineFromMem), .sel(CpuAddress[2]));
  // Set set_1: pin names not known; wires that end beside it: CLK, ReadFromSet0, WriteToSet0, MemToSet0, TagToSet0, OffsetToSet0, LineIterator, LineIterator, Set0Contains, Set0DirtyBit, Set0ByteRead, Set0StoreTag, Set0Line2Mem, WhichLineSet0
  // Set Set1: pin names not known; wires that end beside it: CLK, ReadFromSet1, WriteToSet1, MemToSet1, TagToSet1, OffsetToSet1, LineIterator, LineIterator, Set1Contains, Set1DirtyBit, Set1ByteRead, Set1StoreTag, Set1Line2Mem, WhichLineSet1
  Multiplexer #(.width(8), .enable("false")) multiplexer_1 (
    .in0(Set0ByteRead), .in1(Set1ByteRead), .out(ByteRead), .sel(CpuAddress[2]));
  Multiplexer #(.enable("false")) multiplexer_2 (
    .in0(Set0Contains), .in1(Set1Contains), .out(DidContain), .sel(CpuAddress[2]));
  Multiplexer #(.width(7), .enable("false")) multiplexer_3 (
    .in0(Set0StoreTag), .in1(Set1StoreTag), .out(MemAddress[7:1]), .sel(CpuAddress[2]));
  Multiplexer #(.width(32), .enable("false")) multiplexer_4 (
    .in0(Set0Line2Mem), .in1(Set1Line2Mem), .out(Line2Mem), .sel(CpuAddress[2]));
  Multiplexer #(.enable("false")) multiplexer_5 (
    .in0(Set0DirtyBit), .in1(Set1DirtyBit), .out(DidDirtyBit), .sel(CpuAddress[2]));
  Multiplexer #(.width(3), .enable("false")) multiplexer_6 (
    .in0(WhichLineSet0), .in1(WhichLineSet1), .out(WhichLine), .sel(CpuAddress[2]));
  Multiplexer #(.select(3), .width(2), .enable("false")) multiplexer_7 (
    .in0(2'b00), .in1(2'b00), .in2(2'b01), .in4(2'b10), .out(LineIterator), .sel(WhichLine));  // open: in3, in5, in6, in7

  assign MemAddress[0] = 1'b0;

  // Other names for the same wires on the sheet: Set = CpuAddress[2]; Offset[1:0] = CpuAddress[1:0];
  //   Tag[6:0] = CpuAddress[9:3]

  // Notes on the sheet:
  //   Address Bits = 10
  //   (1) Split CPU Address
  //   Line Size = 4
  //   Get coordinates to look inside cache
  //   W = 3
  //   (2) Using Set: feed the Offset, Tag, CpuRead, and CpuWrite to the right set
  //   Num Sets = 2
  //   C =4*3*2 = 24bytes
  //   Tag bits = 7
endmodule

module Inputs (
  input  HaltTesting,
  input  Ready,
  input  CLK,
  output Done,
  output Read,
  output Write,
  output [9:0] Address,
  output [7:0] Value,
  output [9:0] TestNumber
);

  wire and_1_out, not_1_out, not_2_out;

  not not_1 (not_1_out, HaltTesting);
  not not_2 (not_2_out, Done);
  Counter #(.width(10), .max('h3ff), .ongoal("stay")) u_TestNumber (
    .count(and_1_out), .Q(TestNumber), .clk(CLK));  // open: load, D, carry, clr
  and and_1 (and_1_out, not_1_out, Ready, not_2_out);
  ROM #(.addrWidth(10), .dataWidth(21)) rom_1 (
    .addr(TestNumber), .data({Done, Read, Write, Address, Value}));  // open: sel

  // Notes on the sheet:
  //   contents of rom_1 (hex, n*v repeats v):
  //   40005 40106 40307 40308 41009 4110a 4130b 4130c 4200d 4210e 4230f 42310 43011 43112 43313 43314
  //   44015 44116 44317 44318 45019 4511a 4531b 4531c 80000 80100 80300 80300 81000 81100 81300 81300
  //   82000 82100 82300 82300 83000 83100 83300 83300 84000 84100 84300 84300 85000 85100 85300 85300 0
  //   100000
endmodule

module Checker (
  input  [9:0] TestNumber,
  input  [7:0] YourByteRead,
  output CmdIsRead,
  output [7:0] CorrectByteRead,
  output Correct
);

  wire comparator_1_eq;
  wire [9:0] subtractor_1_out;

  // Probe on TestNumber
  Subtractor #(.width(10)) subtractor_1 (.a(TestNumber), .b(10'h1), .out(subtractor_1_out));  // open: bin, bout
  ROM #(.addrWidth(10), .dataWidth(9)) rom_1 (
    .addr(subtractor_1_out), .data({CmdIsRead, CorrectByteRead}));  // open: sel
  Comparator #(.mode("unsigned")) comparator_1 (
    .a(YourByteRead), .b(CorrectByteRead), .eq(comparator_1_eq));  // open: gt, lt
  and and_1 (Correct, comparator_1_eq, CmdIsRead);

  // Other names for the same wires on the sheet: Test_Number[9:0] = TestNumber

  // Notes on the sheet:
  //   Read Solutions
  //   contents of rom_1 (hex, n*v repeats v):
  //   5 6 7 8 9 a b c d e f 10 11 12 13 14 15 16 17 18 19 1a 1b 1c 105 106 108 108 109 10a 10c 10c 10d 10e
  //   110 110 111 112 114 114 115 116 118 118 119 11a 11c 11c
endmodule

module Line (
  input  [6:0] TagIn,
  input  UpdateTag,
  input  DirtyBitIn,
  input  UpdateDirtyBit,
  input  ValidIn,
  input  UpdateValid,
  input  [1:0] AgeIn,
  input  UpdateAge,
  input  [1:0] Offset,
  input  CLK,
  input  [7:0] Val0In,
  input  [7:0] Val1In,
  input  [7:0] Val2In,
  input  [7:0] Val3In,
  input  WriteToVal,
  output [6:0] TagOut,
  output DirtyBitOut,
  output ValidOut,
  output [1:0] AgeOut,
  output [7:0] ValueOut,
  output ContainsTag,
  output [31:0] Line2Mem
);

  Register #(.width(7)) register_1 (.D(TagIn), .en(UpdateTag), .Q(TagOut), .clk(CLK));  // open: clr
  Register #(.width(1)) register_2 (.D(DirtyBitIn), .en(UpdateDirtyBit), .Q(DirtyBitOut), .clk(CLK));  // open: clr
  Register #(.width(1)) register_3 (.D(ValidIn), .en(UpdateValid), .Q(ValidOut), .clk(CLK));  // open: clr
  Register #(.width(2)) register_4 (.D(AgeIn), .en(UpdateAge), .Q(AgeOut), .clk(CLK));  // open: clr
  Register Val0 (.D(Val0In), .en(WriteToVal), .Q(Line2Mem[7:0]), .clk(CLK));  // open: clr
  Register Val1 (.D(Val1In), .en(WriteToVal), .Q(Line2Mem[15:8]), .clk(CLK));  // open: clr
  Register Val2 (.D(Val2In), .en(WriteToVal), .Q(Line2Mem[23:16]), .clk(CLK));  // open: clr
  Register Val3 (.D(Val3In), .en(WriteToVal), .Q(Line2Mem[31:24]), .clk(CLK));  // open: clr
  // Probe on Line2Mem[31:24]
  Comparator #(.width(7), .mode("unsigned")) comparator_1 (.a(TagIn), .b(TagOut), .eq(ContainsTag));  // open: gt, lt
  Multiplexer #(.select(2), .width(8), .enable("false")) multiplexer_1 (
    .in0(Line2Mem[7:0]), .in1(Line2Mem[15:8]), .in2(Line2Mem[23:16]), .in3(Line2Mem[31:24]), .out(ValueOut),
    .sel(Offset));

  // Other names for the same wires on the sheet: Val0Out[7:0] = Line2Mem[7:0]; Val1Out[7:0] = Line2Mem[15:8];
  //   Val2Out[7:0] = Line2Mem[23:16]; Val3Out[7:0] = Line2Mem[31:24]

  // Notes on the sheet:
  //   Line returns currently stored Tag, Dirty Bit, Valid, and Age Data
  //   Based on Offset, return the correct Value
endmodule

module nextAge (
  input  Set,
  input  Set_2
);

  Multiplexer #(.select(2), .width(7), .enable("false")) multiplexer_1 ();  // open: in0, in1, in2, in3, out, sel
endmodule

module Set (
  input  CLK,
  input  Read,
  input  Write,
  input  [31:0] LineFromMem,
  input  [6:0] Tag,
  input  [1:0] Offset,
  input  [1:0] LineIterator,
  input  UpdateDirty,
  input  UpdateAge,
  input  UpdateValid,
  output Contains,
  output Dirty,
  output [7:0] ByteRead,
  output [6:0] StoredTag,
  output [31:0] Line2Mem,
  output [2:0] WhichLine
);

  wire and_1_out, and_2_out, and_3_out, ContainsTagLine0, ContainsTagLine1, ContainsTagLine2, DirtyBitLine0,
       DirtyBitLine1, DirtyBitLine2, UpdateAgeLine0, UpdateAgeLine1, UpdateAgeLine2, UpdateDirtyBitLine0,
       UpdateDirtyBitLine1, UpdateDirtyBitLine2, UpdateTagLine0, UpdateTagLine1, UpdateTagLine2,
       UpdateValidLine0, UpdateValidLine1, UpdateValidLine2, ValidLine0, ValidLine1, ValidLine2,
       ValidToLine0, ValidToLine1, ValidToLine2, WriteToValLine0, WriteToValLine1, WriteToValLine2;
  wire [1:0] AgeLine0, AgeLine1, AgeLine2, CurrentAgeLine0, CurrentAgeLine1, CurrentAgeLine2,
       multiplexer_1_out, multiplexer_2_out, multiplexer_3_out, multiplexer_4_out, OffsetToLine0,
       OffsetToLine1, OffsetToLine2, updateage_1_nextage, updateage_2_nextage, updateage_3_nextage,
       updateage_4_nextage;
  wire [2:0] DirtyBit, undriven;
  wire [6:0] TagLine0, TagLine1, TagLine2, TagToLine0, TagToLine1, TagToLine2;
  wire [7:0] Val0ToLine0, Val0ToLine1, Val0ToLine2, Val1ToLine0, Val1ToLine1, Val1ToLine2, Val2ToLine0,
       Val2ToLine1, Val2ToLine2, Val3ToLine0, Val3ToLine1, Val3ToLine2, ValLine0, ValLine1, ValLine2;
  wire [31:0] Line02Mem, Line12Mem, Line22Mem;

  isOldestLine isoldestline_1 ();  // open: LineAge, isOldest
  Demultiplexer #(.select(2), .width(7), .enable("false")) demultiplexer_1 (
    .out0(TagToLine0), .out1(TagToLine1), .out2(TagToLine2), .in(Tag), .sel(LineIterator));  // open: out3
  Demultiplexer #(.select(2), .width(2), .enable("false")) demultiplexer_2 (
    .out0(OffsetToLine0), .out1(OffsetToLine1), .out2(OffsetToLine2), .in(Offset), .sel(LineIterator));  // open: out3
  Demultiplexer #(.select(2), .enable("false")) demultiplexer_3 (
    .out0(UpdateTagLine0), .out1(UpdateTagLine1), .out2(UpdateTagLine2), .in(1'b0), .sel(LineIterator));  // open: out3
  Demultiplexer #(.select(2), .enable("false")) demultiplexer_4 (
    .out0(UpdateDirtyBitLine0), .out1(UpdateDirtyBitLine1), .out2(UpdateDirtyBitLine2), .in(1'b0),
    .sel(LineIterator));  // open: out3
  Demultiplexer #(.select(2), .enable("false")) demultiplexer_5 (
    .out0(ValidToLine0), .out1(ValidToLine1), .out2(ValidToLine2), .in(1'b0), .sel(LineIterator));  // open: out3
  Demultiplexer #(.select(2), .enable("false")) demultiplexer_6 (
    .out0(UpdateValidLine0), .out1(UpdateValidLine1), .out2(UpdateValidLine2), .in(UpdateValid),
    .sel(LineIterator));  // open: out3
  Demultiplexer #(.select(2), .enable("false")) demultiplexer_7 (
    .out0(UpdateAgeLine0), .out1(UpdateAgeLine1), .out2(UpdateAgeLine2), .in(UpdateAge), .sel(LineIterator));  // open: out3
  Demultiplexer #(.select(2), .width(8), .enable("false")) demultiplexer_8 (
    .out0(Val0ToLine0), .out1(Val0ToLine1), .out2(Val0ToLine2), .in(LineFromMem[31:24]), .sel(LineIterator));  // open: out3
  Demultiplexer #(.select(2), .width(8), .enable("false")) demultiplexer_9 (
    .out0(Val1ToLine0), .out1(Val1ToLine1), .out2(Val1ToLine2), .in(LineFromMem[23:16]), .sel(LineIterator));  // open: out3
  Demultiplexer #(.select(2), .width(8), .enable("false")) demultiplexer_10 (
    .out0(Val2ToLine0), .out1(Val2ToLine1), .out2(Val2ToLine2), .in(LineFromMem[15:8]), .sel(LineIterator));  // open: out3
  Demultiplexer #(.select(2), .width(8), .enable("false")) demultiplexer_11 (
    .out0(Val3ToLine0), .out1(Val3ToLine1), .out2(Val3ToLine2), .in(LineFromMem[7:0]), .sel(LineIterator));  // open: out3
  Demultiplexer #(.select(2), .enable("false")) demultiplexer_12 (
    .out0(WriteToValLine0), .out1(WriteToValLine1), .out2(WriteToValLine2), .in(Write), .sel(LineIterator));  // open: out3
  Multiplexer #(.select(2), .width(2), .enable("false")) multiplexer_1 (
    .in0(CurrentAgeLine0), .in1(CurrentAgeLine1), .in2(CurrentAgeLine2), .out(multiplexer_1_out),
    .sel(LineIterator));  // open: in3
  Multiplexer #(.select(2), .width(2), .enable("false")) multiplexer_2 (
    .in0(CurrentAgeLine0), .in1(CurrentAgeLine1), .in2(CurrentAgeLine2), .out(multiplexer_2_out),
    .sel(LineIterator));  // open: in3
  Multiplexer #(.select(2), .width(2), .enable("false")) multiplexer_3 (
    .in0(CurrentAgeLine0), .in1(CurrentAgeLine1), .in2(CurrentAgeLine2), .out(multiplexer_3_out),
    .sel(LineIterator));  // open: in3
  Multiplexer #(.select(2), .width(2), .enable("false")) multiplexer_4 (
    .in0(CurrentAgeLine0), .in1(CurrentAgeLine1), .in2(CurrentAgeLine2), .out(multiplexer_4_out),
    .sel(LineIterator));  // open: in3
  UpdateAge updateage_1 (.currentAge(CurrentAgeLine0), .ageAccessed(multiplexer_1_out), .nextAge(updateage_1_nextage));
  UpdateAge updateage_2 (.currentAge(CurrentAgeLine1), .ageAccessed(multiplexer_2_out), .nextAge(updateage_2_nextage));
  UpdateAge updateage_3 (.currentAge(CurrentAgeLine2), .ageAccessed(multiplexer_3_out), .nextAge(updateage_3_nextage));
  UpdateAge updateage_4 (.currentAge(CurrentAgeLine2), .ageAccessed(multiplexer_4_out), .nextAge(updateage_4_nextage));
  Multiplexer #(.width(6), .enable("false")) multiplexer_5 (
    .in0(6'b100100), .in1({updateage_3_nextage, updateage_2_nextage, updateage_1_nextage}),
    .out({AgeLine2, AgeLine1, AgeLine0}), .sel(UpdateAge));
  Multiplexer #(.width(3), .enable("false")) multiplexer_6 (
    .in0(3'b000), .in1(undriven), .out(DirtyBit), .sel(UpdateDirty));
  // Probe on TagLine0
  Line Line0 (
    .TagIn(TagToLine0), .UpdateTag(UpdateTagLine0), .DirtyBitIn(DirtyBit[0]),
    .UpdateDirtyBit(UpdateDirtyBitLine0), .ValidIn(ValidToLine0), .UpdateValid(UpdateValidLine0),
    .AgeIn(AgeLine0), .UpdateAge(UpdateAgeLine0), .Offset(OffsetToLine0), .CLK(CLK), .Val0In(Val0ToLine0),
    .Val1In(Val1ToLine0), .Val2In(Val2ToLine0), .Val3In(Val3ToLine0), .WriteToVal(WriteToValLine0),
    .TagOut(TagLine0), .DirtyBitOut(DirtyBitLine0), .ValidOut(ValidLine0), .AgeOut(CurrentAgeLine0),
    .ValueOut(ValLine0), .ContainsTag(ContainsTagLine0), .Line2Mem(Line02Mem));
  Line Line1 (
    .TagIn(TagToLine1), .UpdateTag(UpdateTagLine1), .DirtyBitIn(DirtyBit[1]),
    .UpdateDirtyBit(UpdateDirtyBitLine1), .ValidIn(ValidToLine1), .UpdateValid(UpdateValidLine1),
    .AgeIn(AgeLine1), .UpdateAge(UpdateAgeLine1), .Offset(OffsetToLine1), .CLK(CLK), .Val0In(Val0ToLine1),
    .Val1In(Val1ToLine1), .Val2In(Val2ToLine1), .Val3In(Val3ToLine1), .WriteToVal(WriteToValLine1),
    .TagOut(TagLine1), .DirtyBitOut(DirtyBitLine1), .ValidOut(ValidLine1), .AgeOut(CurrentAgeLine1),
    .ValueOut(ValLine1), .ContainsTag(ContainsTagLine1), .Line2Mem(Line12Mem));
  Line Line2 (
    .TagIn(TagToLine2), .UpdateTag(UpdateTagLine2), .DirtyBitIn(DirtyBit[2]),
    .UpdateDirtyBit(UpdateDirtyBitLine2), .ValidIn(ValidToLine2), .UpdateValid(UpdateValidLine2),
    .AgeIn(AgeLine2), .UpdateAge(UpdateAgeLine2), .Offset(OffsetToLine2), .CLK(CLK), .Val0In(Val0ToLine2),
    .Val1In(Val1ToLine2), .Val2In(Val2ToLine2), .Val3In(Val3ToLine2), .WriteToVal(WriteToValLine2),
    .TagOut(TagLine2), .DirtyBitOut(DirtyBitLine2), .ValidOut(ValidLine2), .AgeOut(CurrentAgeLine2),
    .ValueOut(ValLine2), .ContainsTag(ContainsTagLine2), .Line2Mem(Line22Mem));
  Multiplexer #(.select(2), .enable("false")) multiplexer_7 (
    .in0(DirtyBitLine0), .in1(DirtyBitLine1), .in2(DirtyBitLine1), .out(Dirty), .sel(LineIterator));  // open: in3
  Multiplexer #(.select(2), .width(8), .enable("false")) multiplexer_8 (
    .in0(ValLine0), .in1(ValLine1), .in2(ValLine2), .out(ByteRead), .sel(LineIterator));  // open: in3
  Multiplexer #(.select(2), .width(7), .enable("false")) multiplexer_9 (
    .in0(TagLine0), .in1(TagLine1), .in2(TagLine2), .out(StoredTag), .sel(LineIterator));  // open: in3
  Multiplexer #(.select(2), .width(32), .enable("false")) multiplexer_10 (
    .in0(Line02Mem), .in1(Line12Mem), .in2(Line22Mem), .out(Line2Mem), .sel(LineIterator));  // open: in3
  and and_1 (and_1_out, ContainsTagLine0, ValidLine0);
  or or_1 (Contains, and_1_out, and_2_out, and_3_out);
  and and_2 (and_2_out, ContainsTagLine1, ValidLine1);
  and and_3 (and_3_out, ContainsTagLine2, ValidLine2);
  Multiplexer #(.width(3), .enable("false")) multiplexer_11 (
    .in0(3'b000), .in1({ContainsTagLine2, ContainsTagLine1, ContainsTagLine0}), .out(WhichLine),
    .sel(Contains));
  // also tied to GND on the sheet: UpdateValid

  // Other names for the same wires on the sheet: Ages[5:0] = {AgeLine2, AgeLine1, AgeLine0};
  //   DirtyBitToLine0 = DirtyBit[0]; DirtyBitToLine1 = DirtyBit[1]; DirtyBitToLine2 = DirtyBit[2];
  //   Val3[7:0] = LineFromMem[7:0]; Val2[7:0] = LineFromMem[15:8]; Val1[7:0] = LineFromMem[23:16];
  //   Val0[7:0] = LineFromMem[31:24]; WriteToVal = Write

  // Notes on the sheet:
  //   FSM Outputs/Inputs
  //   INPUTS
  //   FUNCTIONS
  //   FSM
  //   run findblock to evict state cycles
  //   FSN: if !contains any line
endmodule

module Test (
  input  [6:0] UpdateTag,
  input  UpdateTag_2,
  input  DirtyBitIn,
  input  UpdateDirtyBit,
  input  ValidIn,
  input  UpdateValid,
  input  [1:0] Age,
  input  UpdateAge,
  input  [1:0] Offset,
  input  [7:0] Val0In,
  input  [7:0] Val1In,
  input  [7:0] Val2In,
  input  [7:0] Val3In,
  input  WriteToVal,
  output [6:0] Tag,
  output DirtyBit,
  output Valid,
  output [1:0] Age_2,
  output [7:0] Val,
  output ContainsTag
);

  wire clock_1_out;

  Clock clock_1 (.out(clock_1_out));
  Line line_1 (
    .TagIn(UpdateTag), .UpdateTag(UpdateTag_2), .DirtyBitIn(DirtyBitIn), .UpdateDirtyBit(UpdateDirtyBit),
    .ValidIn(ValidIn), .UpdateValid(UpdateValid), .AgeIn(Age), .UpdateAge(UpdateAge), .Offset(Offset),
    .CLK(clock_1_out), .Val0In(Val0In), .Val1In(Val1In), .Val2In(Val2In), .Val3In(Val3In),
    .WriteToVal(WriteToVal), .TagOut(Tag), .DirtyBitOut(DirtyBit), .ValidOut(Valid), .AgeOut(Age_2),
    .ValueOut(Val), .ContainsTag(ContainsTag));  // open: Line2Mem
  Set set_1 ();  // open: CLK, Read, Write, LineFromMem, Tag, Offset, LineIterator, UpdateDirty, UpdateAge, UpdateValid, Contains, Dirty, ByteRead, StoredTag, Line2Mem, WhichLine
endmodule

module UpdateAge (
  input  [1:0] currentAge,
  input  [1:0] ageAccessed,
  output [1:0] nextAge
);

  wire equal, greater, less;
  wire [1:0] adder_1_out, flag;

  Adder #(.width(2)) adder_1 (.a(currentAge), .b(2'b01), .out(adder_1_out));  // open: cin, cout
  Comparator #(.width(2), .mode("unsigned")) comparator_1 (
    .a(currentAge), .b(ageAccessed), .gt(greater), .eq(equal), .lt(less));
  Multiplexer #(.select(2), .width(2), .enable("false")) multiplexer_1 (
    .in0(2'b00), .in1(currentAge), .in2(adder_1_out), .out(nextAge), .sel(flag));  // open: in3
  comparationConverter comparationconverter_1 (
    .greater(greater), .equal(equal), .less(less), .flag1(flag[1]), .flag0(flag[0]));
  // Probe on flag
endmodule

module comparationConverter (
  input  greater,
  input  equal,
  input  less,
  output flag1,
  output flag0
);


  assign flag0 = greater;
  assign flag1 = less;
endmodule

module isOldestLine (
  input  [1:0] LineAge,
  output isOldest
);

  Comparator #(.width(2), .mode("unsigned")) comparator_1 (.a(LineAge), .b(2'b10), .eq(isOldest));  // open: gt, lt
endmodule

module Read_Write (
  input  LineIterator_0,
  input  Line0Contains,
  input  LineIterator_1,
  input  Line1Contains,
  input  LineIterator_2,
  input  Line2Contains
);

  // AND_Gate and_1 has open pins: in0=LineIterator_0, in1=Line0Contains, out=open
endmodule

module nextState (
  input  prevState3,
  input  prevState2,
  input  prevState1,
  input  prevState0,
  input  ready,
  input  valid,
  input  dirty,
  input  updateAge,
  input  contains,
  input  allValid,
  input  CpuRead,
  input  CpuWrite,
  output nextState3,
  output nextState2,
  output nextState1,
  output nextState0,
  output ready2,
  output valid2,
  output dirty2,
  output updateAge2,
  output contains2,
  output allValid2,
  output CpuRead2,
  output CpuWrite2
);


  assign nextState1 = 1'b0;
endmodule
